# Fritzing sketch Meteostation (saved by Fritzing 0.9.3b)
breadboards: 1

parts:
  Часть1 = Arduino Uno (Rev3)
  LCM1602_IIC1 = LCM1602 IIC [part_number="LCM1602 IIC" chip_label="LCM1602 IIC" package="DIP (Dual Inline) [THT]"]
  LCD1 = LCD screen
  DHT1 = DHT22 Humidity and Temperature Sensor
  R1 = Resistor [tolerance=±5% resistance=10k package="2512 [SMD]"]

nets:
  N1: Часть1.A4/SDA, LCM1602_IIC1.SDA
  N2: Часть1.A5/SCL, LCM1602_IIC1.SCL
  N3: Часть1.D2, DHT1.DATA, R1.Pin_0
  5V: Часть1.5V, LCM1602_IIC1.VCC, DHT1.VDD, R1.Pin_1
  GND: Часть1.GND, LCM1602_IIC1.GND, DHT1.GND
  VSS: LCM1602_IIC1.VSS, LCD1.VSS
  VDD: LCM1602_IIC1.VDD, LCD1.VDD
  N4: LCM1602_IIC1.V0, LCD1.V0
  N5: LCM1602_IIC1.RS, LCD1.RS
  N6: LCM1602_IIC1.RW, LCD1.R/W
  N7: LCM1602_IIC1.E, LCD1.E
  N8: LCM1602_IIC1.D0, LCD1.DB0
  N9: LCM1602_IIC1.D1, LCD1.DB1
  N10: LCM1602_IIC1.D2, LCD1.DB2
  N11: LCM1602_IIC1.D3, LCD1.DB3
  N12: LCM1602_IIC1.D4, LCD1.DB4
  N13: LCM1602_IIC1.D5, LCD1.DB5
  N14: LCM1602_IIC1.D6, LCD1.DB6
  N15: LCM1602_IIC1.D7, LCD1.DB7
  N16: LCM1602_IIC1.A, LCD1.LED+
  N17: LCM1602_IIC1.K, LCD1.LED-
  N18: LCM1602_IIC1.LED_A, LCM1602_IIC1.LED_B

custom parts:
  LCM1602 IIC: I2C-Module to use a 1602 or 2004 LCD on with the wire.h libory Serial LCD Modul
